// Logisim project main.circ as structural Verilog: 6 circuits, main circuit main
module main (
  input  A,
  input  B,
  input  C,
  input  D,
  input  in_5
);

  wire and_1_out, and_2_out, clock_1_out, d_ff_1_q, decoder_1_out0, decoder_1_out1, decoder_1_out2,
       decoder_1_out3, decoder_1_out4, decoder_1_out5, decoder_1_out6, decoder_1_out7, decoder_1_out8,
       decoder_1_out9, decoder_1_out10, decoder_1_out11, decoder_1_out12, decoder_1_out13, decoder_1_out14,
       decoder_1_out15, decodificador_display_1_a_2, decodificador_display_1_b_2,
       decodificador_display_1_c_2, decodificador_display_1_d_2, decodificador_display_1_e,
       decodificador_display_1_f, decodificador_display_1_g, decodificador_display_2_a_2,
       decodificador_display_2_b_2, decodificador_display_2_c_2, decodificador_display_2_d_2,
       decodificador_display_2_e, decodificador_display_2_f, decodificador_display_2_g,
       detector_de_final_1_end, H_a_2, H_b_2, H_c_2, H_d_2, H_e, H_f, H_g, mantener_display_prendido_1_a_2,
       mantener_display_prendido_1_b_2, mantener_display_prendido_1_c_2, mantener_display_prendido_1_d_2,
       mantener_display_prendido_1_e, mantener_display_prendido_1_f, mantener_display_prendido_1_g,
       mantener_display_prendido_2_a_2, mantener_display_prendido_2_b_2, mantener_display_prendido_2_c_2,
       mantener_display_prendido_2_d_2, mantener_display_prendido_2_e, mantener_display_prendido_2_f,
       mantener_display_prendido_2_g, mantener_display_prendido_3_a_2, mantener_display_prendido_3_b_2,
       mantener_display_prendido_3_c_2, mantener_display_prendido_3_d_2, mantener_display_prendido_3_e,
       mantener_display_prendido_3_f, mantener_display_prendido_3_g, mantener_display_prendido_4_a_2,
       mantener_display_prendido_4_b_2, mantener_display_prendido_4_c_2, mantener_display_prendido_4_d_2,
       mantener_display_prendido_4_e, mantener_display_prendido_4_f, mantener_display_prendido_4_g,
       mantener_display_prendido_5_a_2, mantener_display_prendido_5_b_2, mantener_display_prendido_5_c_2,
       mantener_display_prendido_5_d_2, mantener_display_prendido_5_e, mantener_display_prendido_5_f,
       mantener_display_prendido_5_g, mantener_display_prendido_6_a_2, mantener_display_prendido_6_b_2,
       mantener_display_prendido_6_c_2, mantener_display_prendido_6_d_2, mantener_display_prendido_6_e,
       mantener_display_prendido_6_f, mantener_display_prendido_6_g, mantener_display_prendido_7_a_2,
       mantener_display_prendido_7_b_2, mantener_display_prendido_7_c_2, mantener_display_prendido_7_d_2,
       mantener_display_prendido_7_e, mantener_display_prendido_7_f, mantener_display_prendido_7_g,
       mantener_display_prendido_8_a_2, mantener_display_prendido_8_b_2, mantener_display_prendido_8_c_2,
       mantener_display_prendido_8_d_2, mantener_display_prendido_8_e, mantener_display_prendido_8_f,
       mantener_display_prendido_8_g, mantener_display_prendido_9_a_2, mantener_display_prendido_9_b_2,
       mantener_display_prendido_9_c_2, mantener_display_prendido_9_d_2, mantener_display_prendido_9_e,
       mantener_display_prendido_9_f, mantener_display_prendido_9_g, mantener_display_prendido_10_a_2,
       mantener_display_prendido_10_b_2, mantener_display_prendido_10_c_2, mantener_display_prendido_10_d_2,
       mantener_display_prendido_10_e, mantener_display_prendido_10_f, mantener_display_prendido_10_g,
       mantener_display_prendido_11_a_2, mantener_display_prendido_11_b_2, mantener_display_prendido_11_c_2,
       mantener_display_prendido_11_d_2, mantener_display_prendido_11_e, mantener_display_prendido_11_f,
       mantener_display_prendido_11_g, mantener_display_prendido_12_a_2, mantener_display_prendido_12_b_2,
       mantener_display_prendido_12_c_2, mantener_display_prendido_12_d_2, mantener_display_prendido_12_e,
       mantener_display_prendido_12_f, mantener_display_prendido_12_g, mantener_display_prendido_13_a_2,
       mantener_display_prendido_13_b_2, mantener_display_prendido_13_c_2, mantener_display_prendido_13_d_2,
       mantener_display_prendido_13_e, mantener_display_prendido_13_f, mantener_display_prendido_13_g,
       mantener_display_prendido_14_a_2, mantener_display_prendido_14_b_2, mantener_display_prendido_14_c_2,
       mantener_display_prendido_14_d_2, mantener_display_prendido_14_e, mantener_display_prendido_14_f,
       mantener_display_prendido_14_g, mantener_display_prendido_15_a_2, mantener_display_prendido_15_b_2,
       mantener_display_prendido_15_c_2, mantener_display_prendido_15_d_2, mantener_display_prendido_15_e,
       mantener_display_prendido_15_f, mantener_display_prendido_15_g, not_1_out, not_2_out;
  wire [3:0] recorrido_grafo_1_d2;

  _7_Segment_Display u_7_segment_display_1 (
    .g(mantener_display_prendido_1_d_2), .f(mantener_display_prendido_1_b_2),
    .a(mantener_display_prendido_1_a_2), .b(mantener_display_prendido_1_c_2),
    .e(mantener_display_prendido_1_e), .d(mantener_display_prendido_1_g), .c(mantener_display_prendido_1_f));  // open: dp
  mantener_display_prendido mantener_display_prendido_1 (
    .a_2(mantener_display_prendido_1_a_2), .b_2(mantener_display_prendido_1_b_2),
    .c_2(mantener_display_prendido_1_c_2), .d_2(mantener_display_prendido_1_d_2),
    .e(mantener_display_prendido_1_e), .f(mantener_display_prendido_1_f), .g(mantener_display_prendido_1_g),
    .A(recorrido_grafo_1_d2[3]), .B(recorrido_grafo_1_d2[2]), .C(recorrido_grafo_1_d2[1]),
    .D(recorrido_grafo_1_d2[0]), .Reset(in_5), .Reloj(and_2_out), .Enable(decoder_1_out5));
  _7_Segment_Display u_7_segment_display_2 (
    .g(decodificador_display_1_d_2), .f(decodificador_display_1_b_2), .a(decodificador_display_1_a_2),
    .b(decodificador_display_1_c_2), .e(decodificador_display_1_e), .d(decodificador_display_1_g),
    .c(decodificador_display_1_f));  // open: dp
  decodificador_display decodificador_display_1 (
    .a_2(decodificador_display_1_a_2), .b_2(decodificador_display_1_b_2), .c_2(decodificador_display_1_c_2),
    .d_2(decodificador_display_1_d_2), .e(decodificador_display_1_e), .f(decodificador_display_1_f),
    .g(decodificador_display_1_g), .A(A), .B(B), .C(C), .D(D));
  _7_Segment_Display u_7_segment_display_3 (
    .g(mantener_display_prendido_2_d_2), .f(mantener_display_prendido_2_b_2),
    .a(mantener_display_prendido_2_a_2), .b(mantener_display_prendido_2_c_2),
    .e(mantener_display_prendido_2_e), .d(mantener_display_prendido_2_g), .c(mantener_display_prendido_2_f));  // open: dp
  mantener_display_prendido mantener_display_prendido_2 (
    .a_2(mantener_display_prendido_2_a_2), .b_2(mantener_display_prendido_2_b_2),
    .c_2(mantener_display_prendido_2_c_2), .d_2(mantener_display_prendido_2_d_2),
    .e(mantener_display_prendido_2_e), .f(mantener_display_prendido_2_f), .g(mantener_display_prendido_2_g),
    .A(recorrido_grafo_1_d2[3]), .B(recorrido_grafo_1_d2[2]), .C(recorrido_grafo_1_d2[1]),
    .D(recorrido_grafo_1_d2[0]), .Reset(in_5), .Reloj(and_2_out), .Enable(decoder_1_out14));
  _7_Segment_Display u_7_segment_display_4 (
    .g(mantener_display_prendido_3_d_2), .f(mantener_display_prendido_3_b_2),
    .a(mantener_display_prendido_3_a_2), .b(mantener_display_prendido_3_c_2),
    .e(mantener_display_prendido_3_e), .d(mantener_display_prendido_3_g), .c(mantener_display_prendido_3_f));  // open: dp
  mantener_display_prendido mantener_display_prendido_3 (
    .a_2(mantener_display_prendido_3_a_2), .b_2(mantener_display_prendido_3_b_2),
    .c_2(mantener_display_prendido_3_c_2), .d_2(mantener_display_prendido_3_d_2),
    .e(mantener_display_prendido_3_e), .f(mantener_display_prendido_3_f), .g(mantener_display_prendido_3_g),
    .A(recorrido_grafo_1_d2[3]), .B(recorrido_grafo_1_d2[2]), .C(recorrido_grafo_1_d2[1]),
    .D(recorrido_grafo_1_d2[0]), .Reset(in_5), .Reloj(and_2_out), .Enable(decoder_1_out15));
  _7_Segment_Display u_7_segment_display_5 (
    .g(H_d_2), .f(H_b_2), .a(H_a_2), .b(H_c_2), .e(H_e), .d(H_g), .c(H_f));  // open: dp
  _7_Segment_Display u_7_segment_display_6 (
    .g(mantener_display_prendido_4_d_2), .f(mantener_display_prendido_4_b_2),
    .a(mantener_display_prendido_4_a_2), .b(mantener_display_prendido_4_c_2),
    .e(mantener_display_prendido_4_e), .d(mantener_display_prendido_4_g), .c(mantener_display_prendido_4_f));  // open: dp
  _7_Segment_Display u_7_segment_display_7 (
    .g(mantener_display_prendido_5_d_2), .f(mantener_display_prendido_5_b_2),
    .a(mantener_display_prendido_5_a_2), .b(mantener_display_prendido_5_c_2),
    .e(mantener_display_prendido_5_e), .d(mantener_display_prendido_5_g), .c(mantener_display_prendido_5_f));  // open: dp
  _7_Segment_Display u_7_segment_display_8 (
    .g(mantener_display_prendido_6_d_2), .f(mantener_display_prendido_6_b_2),
    .a(mantener_display_prendido_6_a_2), .b(mantener_display_prendido_6_c_2),
    .e(mantener_display_prendido_6_e), .d(mantener_display_prendido_6_g), .c(mantener_display_prendido_6_f));  // open: dp
  mantener_display_prendido H (
    .a_2(H_a_2), .b_2(H_b_2), .c_2(H_c_2), .d_2(H_d_2), .e(H_e), .f(H_f), .g(H_g),
    .A(recorrido_grafo_1_d2[3]), .B(recorrido_grafo_1_d2[2]), .C(recorrido_grafo_1_d2[1]),
    .D(recorrido_grafo_1_d2[0]), .Reset(and_2_out), .Reloj(in_5), .Enable(decoder_1_out7));
  mantener_display_prendido mantener_display_prendido_4 (
    .a_2(mantener_display_prendido_4_a_2), .b_2(mantener_display_prendido_4_b_2),
    .c_2(mantener_display_prendido_4_c_2), .d_2(mantener_display_prendido_4_d_2),
    .e(mantener_display_prendido_4_e), .f(mantener_display_prendido_4_f), .g(mantener_display_prendido_4_g),
    .A(recorrido_grafo_1_d2[3]), .B(recorrido_grafo_1_d2[2]), .C(recorrido_grafo_1_d2[1]),
    .D(recorrido_grafo_1_d2[0]), .Reset(in_5), .Reloj(and_2_out), .Enable(decoder_1_out12));
  mantener_display_prendido mantener_display_prendido_5 (
    .a_2(mantener_display_prendido_5_a_2), .b_2(mantener_display_prendido_5_b_2),
    .c_2(mantener_display_prendido_5_c_2), .d_2(mantener_display_prendido_5_d_2),
    .e(mantener_display_prendido_5_e), .f(mantener_display_prendido_5_f), .g(mantener_display_prendido_5_g),
    .A(recorrido_grafo_1_d2[3]), .B(recorrido_grafo_1_d2[2]), .C(recorrido_grafo_1_d2[1]),
    .D(recorrido_grafo_1_d2[0]), .Reset(in_5), .Reloj(and_2_out), .Enable(decoder_1_out13));
  mantener_display_prendido mantener_display_prendido_6 (
    .a_2(mantener_display_prendido_6_a_2), .b_2(mantener_display_prendido_6_b_2),
    .c_2(mantener_display_prendido_6_c_2), .d_2(mantener_display_prendido_6_d_2),
    .e(mantener_display_prendido_6_e), .f(mantener_display_prendido_6_f), .g(mantener_display_prendido_6_g),
    .A(recorrido_grafo_1_d2[3]), .B(recorrido_grafo_1_d2[2]), .C(recorrido_grafo_1_d2[1]),
    .D(recorrido_grafo_1_d2[0]), .Reset(in_5), .Reloj(and_2_out), .Enable(decoder_1_out10));
  Clock clock_1 (.out(clock_1_out));
  and and_1 (and_1_out, clock_1_out, not_1_out);
  Recorrido_grafo recorrido_grafo_1 (
    .A(A), .B(B), .C(C), .D(D), .Reloj(and_1_out), .Reset(in_5), .A2(recorrido_grafo_1_d2[3]),
    .B2(recorrido_grafo_1_d2[2]), .C2(recorrido_grafo_1_d2[1]), .D2(recorrido_grafo_1_d2[0]));
  not not_1 (not_1_out, detector_de_final_1_end);
  _7_Segment_Display u_7_segment_display_9 (
    .g(mantener_display_prendido_7_d_2), .f(mantener_display_prendido_7_b_2),
    .a(mantener_display_prendido_7_a_2), .b(mantener_display_prendido_7_c_2),
    .e(mantener_display_prendido_7_e), .d(mantener_display_prendido_7_g), .c(mantener_display_prendido_7_f));  // open: dp
  mantener_display_prendido mantener_display_prendido_7 (
    .a_2(mantener_display_prendido_7_a_2), .b_2(mantener_display_prendido_7_b_2),
    .c_2(mantener_display_prendido_7_c_2), .d_2(mantener_display_prendido_7_d_2),
    .e(mantener_display_prendido_7_e), .f(mantener_display_prendido_7_f), .g(mantener_display_prendido_7_g),
    .A(recorrido_grafo_1_d2[3]), .B(recorrido_grafo_1_d2[2]), .C(recorrido_grafo_1_d2[1]),
    .D(recorrido_grafo_1_d2[0]), .Reset(in_5), .Reloj(and_2_out), .Enable(decoder_1_out6));
  _7_Segment_Display u_7_segment_display_10 (
    .g(mantener_display_prendido_8_d_2), .f(mantener_display_prendido_8_b_2),
    .a(mantener_display_prendido_8_a_2), .b(mantener_display_prendido_8_c_2),
    .e(mantener_display_prendido_8_e), .d(mantener_display_prendido_8_g), .c(mantener_display_prendido_8_f));  // open: dp
  mantener_display_prendido mantener_display_prendido_8 (
    .a_2(mantener_display_prendido_8_a_2), .b_2(mantener_display_prendido_8_b_2),
    .c_2(mantener_display_prendido_8_c_2), .d_2(mantener_display_prendido_8_d_2),
    .e(mantener_display_prendido_8_e), .f(mantener_display_prendido_8_f), .g(mantener_display_prendido_8_g),
    .A(recorrido_grafo_1_d2[3]), .B(recorrido_grafo_1_d2[2]), .C(recorrido_grafo_1_d2[1]),
    .D(recorrido_grafo_1_d2[0]), .Reset(in_5), .Reloj(and_2_out), .Enable(decoder_1_out9));
  _7_Segment_Display u_7_segment_display_11 (
    .g(mantener_display_prendido_9_d_2), .f(mantener_display_prendido_9_b_2),
    .a(mantener_display_prendido_9_a_2), .b(mantener_display_prendido_9_c_2),
    .e(mantener_display_prendido_9_e), .d(mantener_display_prendido_9_g), .c(mantener_display_prendido_9_f));  // open: dp
  mantener_display_prendido mantener_display_prendido_9 (
    .a_2(mantener_display_prendido_9_a_2), .b_2(mantener_display_prendido_9_b_2),
    .c_2(mantener_display_prendido_9_c_2), .d_2(mantener_display_prendido_9_d_2),
    .e(mantener_display_prendido_9_e), .f(mantener_display_prendido_9_f), .g(mantener_display_prendido_9_g),
    .A(recorrido_grafo_1_d2[3]), .B(recorrido_grafo_1_d2[2]), .C(recorrido_grafo_1_d2[1]),
    .D(recorrido_grafo_1_d2[0]), .Reset(in_5), .Reloj(and_2_out), .Enable(decoder_1_out11));
  LED led_1 (.in(detector_de_final_1_end));
  detector_de_final detector_de_final_1 (
    .A(recorrido_grafo_1_d2[3]), .B(recorrido_grafo_1_d2[2]), .C(recorrido_grafo_1_d2[1]),
    .D(recorrido_grafo_1_d2[0]), .End(detector_de_final_1_end));
  decodificador_display decodificador_display_2 (
    .a_2(decodificador_display_2_a_2), .b_2(decodificador_display_2_b_2), .c_2(decodificador_display_2_c_2),
    .d_2(decodificador_display_2_d_2), .e(decodificador_display_2_e), .f(decodificador_display_2_f),
    .g(decodificador_display_2_g), .A(recorrido_grafo_1_d2[3]), .B(recorrido_grafo_1_d2[2]),
    .C(recorrido_grafo_1_d2[1]), .D(recorrido_grafo_1_d2[0]));
  _7_Segment_Display u_7_segment_display_12 (
    .g(mantener_display_prendido_10_d_2), .f(mantener_display_prendido_10_b_2),
    .a(mantener_display_prendido_10_a_2), .b(mantener_display_prendido_10_c_2),
    .e(mantener_display_prendido_10_e), .d(mantener_display_prendido_10_g), .c(mantener_display_prendido_10_f));  // open: dp
  _7_Segment_Display u_7_segment_display_13 (
    .g(decodificador_display_2_d_2), .f(decodificador_display_2_b_2), .a(decodificador_display_2_a_2),
    .b(decodificador_display_2_c_2), .e(decodificador_display_2_e), .d(decodificador_display_2_g),
    .c(decodificador_display_2_f));  // open: dp
  Decoder #(.select(4), .enable("false")) decoder_1 (
    .out0(decoder_1_out0), .out1(decoder_1_out1), .out2(decoder_1_out2), .out3(decoder_1_out3),
    .out4(decoder_1_out4), .out5(decoder_1_out5), .out6(decoder_1_out6), .out7(decoder_1_out7),
    .out8(decoder_1_out8), .out9(decoder_1_out9), .out10(decoder_1_out10), .out11(decoder_1_out11),
    .out12(decoder_1_out12), .out13(decoder_1_out13), .out14(decoder_1_out14), .out15(decoder_1_out15),
    .sel(recorrido_grafo_1_d2));
  mantener_display_prendido mantener_display_prendido_10 (
    .a_2(mantener_display_prendido_10_a_2), .b_2(mantener_display_prendido_10_b_2),
    .c_2(mantener_display_prendido_10_c_2), .d_2(mantener_display_prendido_10_d_2),
    .e(mantener_display_prendido_10_e), .f(mantener_display_prendido_10_f),
    .g(mantener_display_prendido_10_g), .A(recorrido_grafo_1_d2[3]), .B(recorrido_grafo_1_d2[2]),
    .C(recorrido_grafo_1_d2[1]), .D(recorrido_grafo_1_d2[0]), .Reset(in_5), .Reloj(and_2_out),
    .Enable(decoder_1_out8));
  and and_2 (and_2_out, clock_1_out, not_2_out);
  _7_Segment_Display u_7_segment_display_14 (
    .g(mantener_display_prendido_11_d_2), .f(mantener_display_prendido_11_b_2),
    .a(mantener_display_prendido_11_a_2), .b(mantener_display_prendido_11_c_2),
    .e(mantener_display_prendido_11_e), .d(mantener_display_prendido_11_g), .c(mantener_display_prendido_11_f));  // open: dp
  _7_Segment_Display u_7_segment_display_15 (
    .g(mantener_display_prendido_12_d_2), .f(mantener_display_prendido_12_b_2),
    .a(mantener_display_prendido_12_a_2), .b(mantener_display_prendido_12_c_2),
    .e(mantener_display_prendido_12_e), .d(mantener_display_prendido_12_g), .c(mantener_display_prendido_12_f));  // open: dp
  not not_2 (not_2_out, d_ff_1_q);
  mantener_display_prendido mantener_display_prendido_11 (
    .a_2(mantener_display_prendido_11_a_2), .b_2(mantener_display_prendido_11_b_2),
    .c_2(mantener_display_prendido_11_c_2), .d_2(mantener_display_prendido_11_d_2),
    .e(mantener_display_prendido_11_e), .f(mantener_display_prendido_11_f),
    .g(mantener_display_prendido_11_g), .A(recorrido_grafo_1_d2[3]), .B(recorrido_grafo_1_d2[2]),
    .C(recorrido_grafo_1_d2[1]), .D(recorrido_grafo_1_d2[0]), .Reset(in_5), .Reloj(and_2_out),
    .Enable(decoder_1_out3));
  mantener_display_prendido mantener_display_prendido_12 (
    .a_2(mantener_display_prendido_12_a_2), .b_2(mantener_display_prendido_12_b_2),
    .c_2(mantener_display_prendido_12_c_2), .d_2(mantener_display_prendido_12_d_2),
    .e(mantener_display_prendido_12_e), .f(mantener_display_prendido_12_f),
    .g(mantener_display_prendido_12_g), .A(recorrido_grafo_1_d2[3]), .B(recorrido_grafo_1_d2[2]),
    .C(recorrido_grafo_1_d2[1]), .D(recorrido_grafo_1_d2[0]), .Reset(in_5), .Reloj(and_2_out),
    .Enable(decoder_1_out4));
  D_Flip_Flop d_ff_1 (
    .clk(clock_1_out), .D(detector_de_final_1_end), .Q(d_ff_1_q), .en(1'b1), .reset(in_5));  // open: Qn, preset
  _7_Segment_Display u_7_segment_display_16 (
    .g(mantener_display_prendido_13_d_2), .f(mantener_display_prendido_13_b_2),
    .a(mantener_display_prendido_13_a_2), .b(mantener_display_prendido_13_c_2),
    .e(mantener_display_prendido_13_e), .d(mantener_display_prendido_13_g), .c(mantener_display_prendido_13_f));  // open: dp
  mantener_display_prendido mantener_display_prendido_13 (
    .a_2(mantener_display_prendido_13_a_2), .b_2(mantener_display_prendido_13_b_2),
    .c_2(mantener_display_prendido_13_c_2), .d_2(mantener_display_prendido_13_d_2),
    .e(mantener_display_prendido_13_e), .f(mantener_display_prendido_13_f),
    .g(mantener_display_prendido_13_g), .A(recorrido_grafo_1_d2[3]), .B(recorrido_grafo_1_d2[2]),
    .C(recorrido_grafo_1_d2[1]), .D(recorrido_grafo_1_d2[0]), .Reset(in_5), .Reloj(and_2_out),
    .Enable(decoder_1_out0));
  _7_Segment_Display u_7_segment_display_17 (
    .g(mantener_display_prendido_14_d_2), .f(mantener_display_prendido_14_b_2),
    .a(mantener_display_prendido_14_a_2), .b(mantener_display_prendido_14_c_2),
    .e(mantener_display_prendido_14_e), .d(mantener_display_prendido_14_g), .c(mantener_display_prendido_14_f));  // open: dp
  mantener_display_prendido mantener_display_prendido_14 (
    .a_2(mantener_display_prendido_14_a_2), .b_2(mantener_display_prendido_14_b_2),
    .c_2(mantener_display_prendido_14_c_2), .d_2(mantener_display_prendido_14_d_2),
    .e(mantener_display_prendido_14_e), .f(mantener_display_prendido_14_f),
    .g(mantener_display_prendido_14_g), .A(recorrido_grafo_1_d2[3]), .B(recorrido_grafo_1_d2[2]),
    .C(recorrido_grafo_1_d2[1]), .D(recorrido_grafo_1_d2[0]), .Reset(in_5), .Reloj(and_2_out),
    .Enable(decoder_1_out1));
  _7_Segment_Display u_7_segment_display_18 (
    .g(mantener_display_prendido_15_d_2), .f(mantener_display_prendido_15_b_2),
    .a(mantener_display_prendido_15_a_2), .b(mantener_display_prendido_15_c_2),
    .e(mantener_display_prendido_15_e), .d(mantener_display_prendido_15_g), .c(mantener_display_prendido_15_f));  // open: dp
  mantener_display_prendido mantener_display_prendido_15 (
    .a_2(mantener_display_prendido_15_a_2), .b_2(mantener_display_prendido_15_b_2),
    .c_2(mantener_display_prendido_15_c_2), .d_2(mantener_display_prendido_15_d_2),
    .e(mantener_display_prendido_15_e), .f(mantener_display_prendido_15_f),
    .g(mantener_display_prendido_15_g), .A(recorrido_grafo_1_d2[3]), .B(recorrido_grafo_1_d2[2]),
    .C(recorrido_grafo_1_d2[1]), .D(recorrido_grafo_1_d2[0]), .Reset(in_5), .Reloj(and_2_out),
    .Enable(decoder_1_out2));

  // Notes on the sheet:
  //   F
  //   O
  //   P
  //   H
  //   M
  //   N
  //   K
  //   G
  //   J
  //   L
  //   I
  //   D
  //   E
  //   A
  //   B
  //   C
endmodule

module decodificador_display (
  input  A,
  input  B,
  input  C,
  input  D,
  output a_2,
  output b_2,
  output c_2,
  output d_2,
  output e,
  output f,
  output g
);

  wire and_1_out, and_2_out, and_3_out, and_4_out, and_5_out, and_6_out, and_7_out, and_8_out, and_9_out,
       and_10_out, and_11_out, and_12_out, and_13_out, and_14_out, and_15_out, and_16_out, and_17_out,
       and_18_out, and_19_out, and_20_out, and_21_out, and_22_out, and_23_out, and_24_out, and_25_out,
       and_26_out, and_27_out, and_28_out, and_29_out, and_30_out, and_31_out, and_32_out, and_33_out,
       and_34_out, and_35_out, and_36_out, and_37_out, and_38_out, not_1_out, not_2_out, not_3_out,
       not_4_out, not_5_out, not_6_out, not_7_out, not_8_out, not_9_out, not_10_out, not_11_out, not_12_out,
       not_13_out, not_14_out, not_15_out, not_16_out, not_17_out, not_18_out, not_19_out, not_20_out,
       not_21_out, not_22_out, not_23_out, not_24_out, not_25_out, not_26_out, not_27_out, not_28_out,
       not_29_out, not_30_out, not_31_out, not_32_out, not_33_out, not_34_out, not_35_out, not_36_out,
       or_1_out, or_2_out, or_3_out, or_4_out, or_5_out, or_6_out, or_9_out, or_10_out, or_11_out, or_12_out,
       or_14_out, or_15_out, or_16_out, or_19_out, or_20_out;

  not not_1 (not_1_out, A);
  not not_2 (not_2_out, D);
  not not_3 (not_3_out, D);
  not not_4 (not_4_out, C);
  not not_5 (not_5_out, A);
  not not_6 (not_6_out, C);
  not not_7 (not_7_out, A);
  not not_8 (not_8_out, D);
  not not_9 (not_9_out, A);
  not not_10 (not_10_out, B);
  not not_11 (not_11_out, C);
  not not_12 (not_12_out, A);
  not not_13 (not_13_out, B);
  not not_14 (not_14_out, C);
  not not_15 (not_15_out, B);
  not not_16 (not_16_out, C);
  not not_17 (not_17_out, D);
  not not_18 (not_18_out, A);
  not not_19 (not_19_out, B);
  not not_20 (not_20_out, A);
  not not_21 (not_21_out, B);
  not not_22 (not_22_out, A);
  and and_1 (and_1_out, not_1_out, not_2_out);
  and and_2 (and_2_out, C, not_3_out);
  and and_3 (and_3_out, B, not_4_out);
  and and_4 (and_4_out, A, B);
  and and_5 (and_5_out, not_5_out, not_6_out);
  and and_6 (and_6_out, not_7_out, not_8_out);
  and and_7 (and_7_out, not_9_out, B);
  and and_8 (and_8_out, A, C);
  and and_9 (and_9_out, not_10_out, not_11_out);
  not not_23 (not_23_out, D);
  and and_10 (and_10_out, not_12_out, C);
  and and_11 (and_11_out, A, not_13_out);
  not not_24 (not_24_out, C);
  and and_12 (and_12_out, A, B);
  not not_25 (not_25_out, A);
  not not_26 (not_26_out, C);
  and and_13 (and_13_out, B, not_14_out);
  not not_27 (not_27_out, D);
  and and_14 (and_14_out, A, not_15_out);
  not not_28 (not_28_out, A);
  and and_15 (and_15_out, not_16_out, D);
  and and_16 (and_16_out, C, not_17_out);
  not not_29 (not_29_out, B);
  not not_30 (not_30_out, C);
  and and_17 (and_17_out, not_18_out, not_19_out);
  not not_31 (not_31_out, A);
  not not_32 (not_32_out, B);
  and and_18 (and_18_out, not_20_out, not_21_out);
  and and_19 (and_19_out, not_22_out, B);
  not not_33 (not_33_out, D);
  and and_20 (and_20_out, B, C);
  not not_34 (not_34_out, D);
  or or_1 (or_1_out, and_1_out, and_2_out);
  or or_2 (or_2_out, and_3_out, and_4_out);
  or or_3 (or_3_out, and_5_out, and_6_out);
  or or_4 (or_4_out, and_7_out, and_8_out);
  and and_21 (and_21_out, and_9_out, not_23_out);
  and and_22 (and_22_out, and_10_out, D);
  and and_23 (and_23_out, and_11_out, not_24_out);
  and and_24 (and_24_out, and_12_out, C);
  and and_25 (and_25_out, not_25_out, not_26_out);
  and and_26 (and_26_out, C, D);
  and and_27 (and_27_out, and_13_out, not_27_out);
  and and_28 (and_28_out, and_14_out, C);
  or or_5 (or_5_out, not_28_out, and_15_out);
  or or_6 (or_6_out, and_16_out, B);
  and and_29 (and_29_out, not_29_out, not_30_out);
  and and_30 (and_30_out, and_17_out, D);
  and and_31 (and_31_out, not_31_out, B);
  not not_35 (not_35_out, C);
  not not_36 (not_36_out, D);
  and and_32 (and_32_out, not_32_out, D);
  and and_33 (and_33_out, and_18_out, C);
  and and_34 (and_34_out, and_19_out, not_33_out);
  and and_35 (and_35_out, and_20_out, not_34_out);
  or or_7 (a_2, or_1_out, or_2_out);
  or or_8 (b_2, or_3_out, or_4_out);
  or or_9 (or_9_out, and_21_out, and_22_out);
  or or_10 (or_10_out, and_23_out, and_24_out);
  or or_11 (or_11_out, and_25_out, and_26_out);
  or or_12 (or_12_out, and_27_out, and_28_out);
  or or_13 (e, or_5_out, or_6_out);
  or or_14 (or_14_out, and_29_out, and_30_out);
  and and_36 (and_36_out, and_31_out, C);
  and and_37 (and_37_out, A, not_35_out);
  and and_38 (and_38_out, A, not_36_out);
  or or_15 (or_15_out, and_32_out, and_33_out);
  or or_16 (or_16_out, and_34_out, and_35_out);
  or or_17 (c_2, or_9_out, or_10_out);
  or or_18 (d_2, or_11_out, or_12_out);
  or or_19 (or_19_out, or_14_out, and_36_out);
  or or_20 (or_20_out, and_37_out, and_38_out);
  or or_21 (g, or_15_out, or_16_out);
  or or_22 (f, or_19_out, or_20_out);
  _7_Segment_Display u_7_segment_display_1 (.g(d_2), .f(b_2), .a(a_2), .b(c_2), .e(e), .d(g), .c(f));  // open: dp
endmodule

module mantener_display_prendido (
  input  A,
  input  B,
  input  C,
  input  D,
  input  Reset,
  input  Reloj,
  input  Enable,
  output a_2,
  output b_2,
  output c_2,
  output d_2,
  output e,
  output f,
  output g
);

  wire and_1_out, and_2_out, and_3_out, and_4_out, and_5_out, and_6_out, and_7_out, and_8_out, and_9_out,
       and_10_out, and_11_out, and_12_out, and_13_out, and_14_out, and_15_out, and_16_out, and_17_out,
       and_18_out, and_19_out, and_20_out, and_21_out, and_22_out, and_23_out, and_24_out, and_25_out,
       and_26_out, d_ff_1_q, multiplexer_1_out, multiplexer_2_out, multiplexer_3_out, multiplexer_4_out,
       multiplexer_5_out, multiplexer_6_out, multiplexer_7_out, not_1_out, not_2_out, not_3_out, not_4_out,
       not_5_out, not_6_out, not_7_out, not_8_out, not_9_out, not_10_out, not_11_out, not_12_out, not_13_out,
       not_14_out, not_15_out, not_16_out, not_17_out, not_18_out, not_19_out, not_20_out, not_21_out,
       not_22_out, not_23_out, not_24_out, not_25_out, not_26_out, not_27_out, not_28_out, not_29_out,
       not_30_out, not_31_out, not_32_out, not_33_out, not_34_out, not_35_out, not_36_out, or_1_out,
       or_2_out, or_3_out, or_4_out, or_5_out, or_6_out, or_7_out;

  not not_1 (not_1_out, A);
  not not_2 (not_2_out, D);
  not not_3 (not_3_out, D);
  not not_4 (not_4_out, C);
  not not_5 (not_5_out, A);
  not not_6 (not_6_out, C);
  not not_7 (not_7_out, A);
  not not_8 (not_8_out, D);
  not not_9 (not_9_out, A);
  not not_10 (not_10_out, B);
  not not_11 (not_11_out, C);
  not not_12 (not_12_out, D);
  not not_13 (not_13_out, A);
  not not_14 (not_14_out, B);
  not not_15 (not_15_out, C);
  not not_16 (not_16_out, A);
  not not_17 (not_17_out, C);
  not not_18 (not_18_out, A);
  not not_19 (not_19_out, C);
  not not_20 (not_20_out, D);
  not not_21 (not_21_out, B);
  not not_22 (not_22_out, D);
  not not_23 (not_23_out, A);
  not not_24 (not_24_out, B);
  not not_25 (not_25_out, C);
  not not_26 (not_26_out, A);
  not not_27 (not_27_out, B);
  not not_28 (not_28_out, A);
  not not_29 (not_29_out, C);
  not not_30 (not_30_out, D);
  not not_31 (not_31_out, B);
  not not_32 (not_32_out, A);
  not not_33 (not_33_out, B);
  not not_34 (not_34_out, A);
  not not_35 (not_35_out, D);
  not not_36 (not_36_out, D);
  and and_1 (and_1_out, not_1_out, not_2_out);
  and and_2 (and_2_out, C, not_3_out);
  and and_3 (and_3_out, B, not_4_out);
  and and_4 (and_4_out, A, B);
  and and_5 (and_5_out, not_5_out, not_6_out);
  and and_6 (and_6_out, not_7_out, not_8_out);
  and and_7 (and_7_out, not_9_out, B);
  and and_8 (and_8_out, A, C);
  and and_9 (and_9_out, not_10_out, not_11_out, not_12_out);
  and and_10 (and_10_out, not_13_out, C, D);
  and and_11 (and_11_out, A, not_14_out, not_15_out);
  and and_12 (and_12_out, A, B, C);
  and and_13 (and_13_out, not_16_out, not_17_out);
  and and_14 (and_14_out, not_18_out, D);
  and and_15 (and_15_out, B, not_19_out, not_20_out);
  and and_16 (and_16_out, B, C, D);
  and and_17 (and_17_out, A, not_21_out, C, not_22_out);
  or or_1 (or_1_out, not_23_out, D, C, B);
  and and_18 (and_18_out, not_24_out, not_25_out);
  and and_19 (and_19_out, not_26_out, not_27_out, D);
  and and_20 (and_20_out, not_28_out, B, C);
  and and_21 (and_21_out, A, not_29_out);
  and and_22 (and_22_out, A, not_30_out);
  and and_23 (and_23_out, not_31_out, D);
  and and_24 (and_24_out, not_32_out, not_33_out, C);
  and and_25 (and_25_out, not_34_out, B, not_35_out);
  and and_26 (and_26_out, B, C, not_36_out);
  or or_2 (or_2_out, and_1_out, and_2_out, and_3_out, and_4_out);
  or or_3 (or_3_out, and_5_out, and_6_out, and_7_out, and_8_out);
  or or_4 (or_4_out, and_9_out, and_10_out, and_11_out, and_12_out);
  or or_5 (or_5_out, and_13_out, and_14_out, and_15_out, and_16_out, and_17_out);
  or or_6 (or_6_out, and_18_out, and_19_out, and_20_out, and_21_out, and_22_out);
  or or_7 (or_7_out, and_23_out, and_24_out, and_25_out, and_26_out);
  D_Flip_Flop d_ff_1 (.clk(Reloj), .D(1'b1), .Q(d_ff_1_q), .en(Enable), .reset(Reset));  // open: Qn, preset
  Multiplexer #(.enable("false")) multiplexer_1 (.in0(or_2_out), .in1(a_2), .out(multiplexer_1_out), .sel(d_ff_1_q));
  Multiplexer #(.enable("false")) multiplexer_2 (.in0(or_3_out), .in1(b_2), .out(multiplexer_2_out), .sel(d_ff_1_q));
  Multiplexer #(.enable("false")) multiplexer_3 (.in0(or_4_out), .in1(c_2), .out(multiplexer_3_out), .sel(d_ff_1_q));
  Multiplexer #(.enable("false")) multiplexer_4 (.in0(or_5_out), .in1(d_2), .out(multiplexer_4_out), .sel(d_ff_1_q));
  Multiplexer #(.enable("false")) multiplexer_5 (.in0(or_1_out), .in1(e), .out(multiplexer_5_out), .sel(d_ff_1_q));
  Multiplexer #(.enable("false")) multiplexer_6 (.in0(or_6_out), .in1(f), .out(multiplexer_6_out), .sel(d_ff_1_q));
  Multiplexer #(.enable("false")) multiplexer_7 (.in0(or_7_out), .in1(g), .out(multiplexer_7_out), .sel(d_ff_1_q));
  D_Flip_Flop d_ff_2 (.clk(Reloj), .D(multiplexer_1_out), .Q(a_2), .en(Enable), .reset(Reset));  // open: Qn, preset
  D_Flip_Flop d_ff_3 (.clk(Reloj), .D(multiplexer_2_out), .Q(b_2), .en(Enable), .reset(Reset));  // open: Qn, preset
  D_Flip_Flop d_ff_4 (.clk(Reloj), .D(multiplexer_3_out), .Q(c_2), .en(Enable), .reset(Reset));  // open: Qn, preset
  D_Flip_Flop d_ff_5 (.clk(Reloj), .D(multiplexer_4_out), .Q(d_2), .en(Enable), .reset(Reset));  // open: Qn, preset
  D_Flip_Flop d_ff_6 (.clk(Reloj), .D(multiplexer_5_out), .Q(e), .en(Enable), .reset(Reset));  // open: Qn, preset
  D_Flip_Flop d_ff_7 (.clk(Reloj), .D(multiplexer_6_out), .Q(f), .en(Enable), .reset(Reset));  // open: Qn, preset
  D_Flip_Flop d_ff_8 (.clk(Reloj), .D(multiplexer_7_out), .Q(g), .en(Enable), .reset(Reset));  // open: Qn, preset
endmodule

module detector_de_final (
  input  A,
  input  B,
  input  C,
  input  D,
  output End
);

  wire not_1_out, not_2_out;

  not not_1 (not_1_out, A);
  not not_2 (not_2_out, C);
  and and_1 (End, not_1_out, B, not_2_out, D);
endmodule

module nodo_siguiente (
  input  A1,
  input  A2,
  input  A3,
  input  A4,
  output B1,
  output B2,
  output B3,
  output B4
);

  wire and_1_out, and_2_out, and_3_out, and_4_out, and_5_out, and_6_out, and_7_out, and_8_out, and_9_out,
       and_10_out, and_11_out, and_12_out, and_13_out, and_14_out, and_15_out, and_16_out, and_17_out,
       and_18_out, and_19_out, and_20_out, and_21_out, and_22_out, decodificador_display_1_a_2,
       decodificador_display_1_b_2, decodificador_display_1_c_2, decodificador_display_1_d_2,
       decodificador_display_1_e, decodificador_display_1_f, decodificador_display_1_g,
       decodificador_display_2_a_2, decodificador_display_2_b_2, decodificador_display_2_c_2,
       decodificador_display_2_d_2, decodificador_display_2_e, decodificador_display_2_f,
       decodificador_display_2_g, not_1_out, not_2_out, not_3_out, not_4_out, not_5_out, not_6_out,
       not_7_out, not_8_out, not_9_out, not_10_out, not_11_out, not_12_out, not_13_out, not_14_out,
       not_15_out, not_16_out, or_1_out, or_2_out, or_3_out, or_4_out, or_5_out, or_7_out, or_8_out, or_9_out;

  _7_Segment_Display u_7_segment_display_1 (
    .g(decodificador_display_1_d_2), .f(decodificador_display_1_b_2), .a(decodificador_display_1_a_2),
    .b(decodificador_display_1_c_2), .e(decodificador_display_1_e), .d(decodificador_display_1_g),
    .c(decodificador_display_1_f));  // open: dp
  decodificador_display decodificador_display_1 (
    .a_2(decodificador_display_1_a_2), .b_2(decodificador_display_1_b_2), .c_2(decodificador_display_1_c_2),
    .d_2(decodificador_display_1_d_2), .e(decodificador_display_1_e), .f(decodificador_display_1_f),
    .g(decodificador_display_1_g), .A(A1), .B(A2), .C(A3), .D(A4));
  not not_1 (not_1_out, A1);
  and and_1 (and_1_out, A2, A4);
  and and_2 (and_2_out, A2, A3);
  not not_2 (not_2_out, A1);
  not not_3 (not_3_out, A2);
  not not_4 (not_4_out, A3);
  not not_5 (not_5_out, A1);
  not not_6 (not_6_out, A1);
  not not_7 (not_7_out, A3);
  not not_8 (not_8_out, A1);
  not not_9 (not_9_out, A4);
  not not_10 (not_10_out, A3);
  and and_3 (and_3_out, not_1_out, A3);
  not not_11 (not_11_out, A2);
  or or_1 (or_1_out, and_1_out, and_2_out);
  and and_4 (and_4_out, A1, A4);
  and and_5 (and_5_out, A1, A3);
  and and_6 (and_6_out, A1, A2);
  and and_7 (and_7_out, not_2_out, not_3_out);
  and and_8 (and_8_out, not_4_out, A4);
  and and_9 (and_9_out, not_5_out, A2);
  not not_12 (not_12_out, A4);
  and and_10 (and_10_out, not_6_out, not_7_out);
  and and_11 (and_11_out, not_8_out, not_9_out);
  not not_13 (not_13_out, A2);
  not not_14 (not_14_out, A4);
  and and_12 (and_12_out, A2, not_10_out);
  and and_13 (and_13_out, and_3_out, A4);
  and and_14 (and_14_out, A1, not_11_out);
  not not_15 (not_15_out, A3);
  or or_2 (or_2_out, or_1_out, and_4_out);
  or or_3 (or_3_out, and_5_out, and_6_out);
  and and_15 (and_15_out, and_7_out, and_8_out);
  and and_16 (and_16_out, and_9_out, not_12_out);
  and and_17 (and_17_out, A1, A2);
  not not_16 (not_16_out, A3);
  or or_4 (or_4_out, and_10_out, and_11_out);
  and and_18 (and_18_out, not_13_out, not_14_out);
  and and_19 (and_19_out, and_12_out, A4);
  and and_20 (and_20_out, A1, A3);
  or or_5 (or_5_out, and_13_out, and_14_out);
  and and_21 (and_21_out, A1, not_15_out);
  or or_6 (B2, or_2_out, or_3_out);
  or or_7 (or_7_out, and_15_out, and_16_out);
  and and_22 (and_22_out, and_17_out, not_16_out);
  or or_8 (or_8_out, or_4_out, and_18_out);
  or or_9 (or_9_out, and_19_out, and_20_out);
  or or_10 (B1, or_5_out, and_21_out);
  or or_11 (B3, or_7_out, and_22_out);
  or or_12 (B4, or_8_out, or_9_out);
  decodificador_display decodificador_display_2 (
    .a_2(decodificador_display_2_a_2), .b_2(decodificador_display_2_b_2), .c_2(decodificador_display_2_c_2),
    .d_2(decodificador_display_2_d_2), .e(decodificador_display_2_e), .f(decodificador_display_2_f),
    .g(decodificador_display_2_g), .A(B1), .B(B2), .C(B3), .D(B4));
  _7_Segment_Display u_7_segment_display_2 (
    .g(decodificador_display_2_d_2), .f(decodificador_display_2_b_2), .a(decodificador_display_2_a_2),
    .b(decodificador_display_2_c_2), .e(decodificador_display_2_e), .d(decodificador_display_2_g),
    .c(decodificador_display_2_f));  // open: dp

  // Notes on the sheet:
  //   Nodo Actual
  //   Nodo siguiente
endmodule

module Recorrido_grafo (
  input  A,
  input  B,
  input  C,
  input  D,
  input  Reloj,
  input  Reset,
  output A2,
  output B2,
  output C2,
  output D2
);

  wire d_ff_1_q, d_ff_2_q, d_ff_3_q, d_ff_4_q, d_ff_5_q, decodificador_display_1_a_2,
       decodificador_display_1_b_2, decodificador_display_1_c_2, decodificador_display_1_d_2,
       decodificador_display_1_e, decodificador_display_1_f, decodificador_display_1_g,
       decodificador_display_2_a_2, decodificador_display_2_b_2, decodificador_display_2_c_2,
       decodificador_display_2_d_2, decodificador_display_2_e, decodificador_display_2_f,
       decodificador_display_2_g, multiplexer_5_out, multiplexer_6_out, multiplexer_7_out, multiplexer_8_out,
       nodo_siguiente_1_b1, nodo_siguiente_1_b2, nodo_siguiente_1_b3, nodo_siguiente_1_b4;

  decodificador_display decodificador_display_1 (
    .a_2(decodificador_display_1_a_2), .b_2(decodificador_display_1_b_2), .c_2(decodificador_display_1_c_2),
    .d_2(decodificador_display_1_d_2), .e(decodificador_display_1_e), .f(decodificador_display_1_f),
    .g(decodificador_display_1_g), .A(A), .B(B), .C(C), .D(D));
  _7_Segment_Display u_7_segment_display_1 (
    .g(decodificador_display_1_d_2), .f(decodificador_display_1_b_2), .a(decodificador_display_1_a_2),
    .b(decodificador_display_1_c_2), .e(decodificador_display_1_e), .d(decodificador_display_1_g),
    .c(decodificador_display_1_f));  // open: dp
  decodificador_display decodificador_display_2 (
    .a_2(decodificador_display_2_a_2), .b_2(decodificador_display_2_b_2), .c_2(decodificador_display_2_c_2),
    .d_2(decodificador_display_2_d_2), .e(decodificador_display_2_e), .f(decodificador_display_2_f),
    .g(decodificador_display_2_g), .A(A2), .B(B2), .C(C2), .D(D2));
  _7_Segment_Display u_7_segment_display_2 (
    .g(decodificador_display_2_d_2), .f(decodificador_display_2_b_2), .a(decodificador_display_2_a_2),
    .b(decodificador_display_2_c_2), .e(decodificador_display_2_e), .d(decodificador_display_2_g),
    .c(decodificador_display_2_f));  // open: dp
  D_Flip_Flop d_ff_1 (.clk(Reloj), .D(1'b1), .Q(d_ff_1_q), .en(1'b1), .reset(Reset));  // open: Qn, preset
  Multiplexer #(.enable("false")) multiplexer_1 (.in0(A), .in1(nodo_siguiente_1_b1), .out(A2), .sel(d_ff_1_q));
  Multiplexer #(.enable("false")) multiplexer_2 (.in0(B), .in1(nodo_siguiente_1_b2), .out(B2), .sel(d_ff_1_q));
  Multiplexer #(.enable("false")) multiplexer_3 (.in0(C), .in1(nodo_siguiente_1_b3), .out(C2), .sel(d_ff_1_q));
  Multiplexer #(.enable("false")) multiplexer_4 (.in0(D), .in1(nodo_siguiente_1_b4), .out(D2), .sel(d_ff_1_q));
  Multiplexer #(.enable("false")) multiplexer_5 (
    .in0(D), .in1(nodo_siguiente_1_b4), .out(multiplexer_5_out), .sel(d_ff_1_q));
  Multiplexer #(.enable("false")) multiplexer_6 (
    .in0(C), .in1(nodo_siguiente_1_b3), .out(multiplexer_6_out), .sel(d_ff_1_q));
  Multiplexer #(.enable("false")) multiplexer_7 (
    .in0(B), .in1(nodo_siguiente_1_b2), .out(multiplexer_7_out), .sel(d_ff_1_q));
  Multiplexer #(.enable("false")) multiplexer_8 (
    .in0(A), .in1(nodo_siguiente_1_b1), .out(multiplexer_8_out), .sel(d_ff_1_q));
  D_Flip_Flop d_ff_2 (.clk(Reloj), .D(multiplexer_5_out), .Q(d_ff_2_q), .en(1'b1), .reset(Reset));  // open: Qn, preset
  D_Flip_Flop d_ff_3 (.clk(Reloj), .D(multiplexer_6_out), .Q(d_ff_3_q), .en(1'b1), .reset(Reset));  // open: Qn, preset
  D_Flip_Flop d_ff_4 (.clk(Reloj), .D(multiplexer_7_out), .Q(d_ff_4_q), .en(1'b1), .reset(Reset));  // open: Qn, preset
  D_Flip_Flop d_ff_5 (.clk(Reloj), .D(multiplexer_8_out), .Q(d_ff_5_q), .en(1'b1), .reset(Reset));  // open: Qn, preset
  nodo_siguiente nodo_siguiente_1 (
    .A1(d_ff_5_q), .A2(d_ff_4_q), .A3(d_ff_3_q), .A4(d_ff_2_q), .B1(nodo_siguiente_1_b1),
    .B2(nodo_siguiente_1_b2), .B3(nodo_siguiente_1_b3), .B4(nodo_siguiente_1_b4));

  // Notes on the sheet:
  //   Nodo decodificado
  //   Bits de Entrada
endmodule
