// Logisim project mapa.circ as structural Verilog: 6 circuits, main circuit main
// display_decoder
module main (
  input  Reset,
  input  A,
  input  B,
  input  C,
  input  D
);

  wire and_1_out, d_ff_1_q, decoder_1_out0, decoder_1_out1, decoder_1_out2, decoder_1_out3, decoder_1_out4,
       decoder_1_out5, decoder_1_out6, decoder_1_out7, decoder_1_out8, decoder_1_out9, decoder_1_out10,
       decoder_1_out11, decoder_1_out12, decoder_1_out13, decoder_1_out14, decoder_1_out15,
       decodificador_display_1_a_2, decodificador_display_1_b_2, decodificador_display_1_c_2,
       decodificador_display_1_d_2, decodificador_display_1_e, decodificador_display_1_f,
       decodificador_display_1_g, decodificador_display_2_a_2, decodificador_display_2_b_2,
       decodificador_display_2_c_2, decodificador_display_2_d_2, decodificador_display_2_e,
       decodificador_display_2_f, decodificador_display_2_g, detector_de_final_1_end,
       mantener_siplay_prendido_1_a_2, mantener_siplay_prendido_1_b_2, mantener_siplay_prendido_1_c_2,
       mantener_siplay_prendido_1_d_2, mantener_siplay_prendido_1_e, mantener_siplay_prendido_1_f,
       mantener_siplay_prendido_1_g, mantener_siplay_prendido_2_a_2, mantener_siplay_prendido_2_b_2,
       mantener_siplay_prendido_2_c_2, mantener_siplay_prendido_2_d_2, mantener_siplay_prendido_2_e,
       mantener_siplay_prendido_2_f, mantener_siplay_prendido_2_g, mantener_siplay_prendido_3_a_2,
       mantener_siplay_prendido_3_b_2, mantener_siplay_prendido_3_c_2, mantener_siplay_prendido_3_d_2,
       mantener_siplay_prendido_3_e, mantener_siplay_prendido_3_f, mantener_siplay_prendido_3_g,
       mantener_siplay_prendido_4_a_2, mantener_siplay_prendido_4_b_2, mantener_siplay_prendido_4_c_2,
       mantener_siplay_prendido_4_d_2, mantener_siplay_prendido_4_e, mantener_siplay_prendido_4_f,
       mantener_siplay_prendido_4_g, mantener_siplay_prendido_5_a_2, mantener_siplay_prendido_5_b_2,
       mantener_siplay_prendido_5_c_2, mantener_siplay_prendido_5_d_2, mantener_siplay_prendido_5_e,
       mantener_siplay_prendido_5_f, mantener_siplay_prendido_5_g, mantener_siplay_prendido_6_a_2,
       mantener_siplay_prendido_6_b_2, mantener_siplay_prendido_6_c_2, mantener_siplay_prendido_6_d_2,
       mantener_siplay_prendido_6_e, mantener_siplay_prendido_6_f, mantener_siplay_prendido_6_g,
       mantener_siplay_prendido_7_a_2, mantener_siplay_prendido_7_b_2, mantener_siplay_prendido_7_c_2,
       mantener_siplay_prendido_7_d_2, mantener_siplay_prendido_7_e, mantener_siplay_prendido_7_f,
       mantener_siplay_prendido_7_g, mantener_siplay_prendido_8_a_2, mantener_siplay_prendido_8_b_2,
       mantener_siplay_prendido_8_c_2, mantener_siplay_prendido_8_d_2, mantener_siplay_prendido_8_e,
       mantener_siplay_prendido_8_f, mantener_siplay_prendido_8_g, mantener_siplay_prendido_9_a_2,
       mantener_siplay_prendido_9_b_2, mantener_siplay_prendido_9_c_2, mantener_siplay_prendido_9_d_2,
       mantener_siplay_prendido_9_e, mantener_siplay_prendido_9_f, mantener_siplay_prendido_9_g,
       mantener_siplay_prendido_10_a_2, mantener_siplay_prendido_10_b_2, mantener_siplay_prendido_10_c_2,
       mantener_siplay_prendido_10_d_2, mantener_siplay_prendido_10_e, mantener_siplay_prendido_10_f,
       mantener_siplay_prendido_10_g, mantener_siplay_prendido_11_a_2, mantener_siplay_prendido_11_b_2,
       mantener_siplay_prendido_11_c_2, mantener_siplay_prendido_11_d_2, mantener_siplay_prendido_11_e,
       mantener_siplay_prendido_11_f, mantener_siplay_prendido_11_g, mantener_siplay_prendido_12_a_2,
       mantener_siplay_prendido_12_b_2, mantener_siplay_prendido_12_c_2, mantener_siplay_prendido_12_d_2,
       mantener_siplay_prendido_12_e, mantener_siplay_prendido_12_f, mantener_siplay_prendido_12_g,
       mantener_siplay_prendido_13_a_2, mantener_siplay_prendido_13_b_2, mantener_siplay_prendido_13_c_2,
       mantener_siplay_prendido_13_d_2, mantener_siplay_prendido_13_e, mantener_siplay_prendido_13_f,
       mantener_siplay_prendido_13_g, mantener_siplay_prendido_14_a_2, mantener_siplay_prendido_14_b_2,
       mantener_siplay_prendido_14_c_2, mantener_siplay_prendido_14_d_2, mantener_siplay_prendido_14_e,
       mantener_siplay_prendido_14_f, mantener_siplay_prendido_14_g, mantener_siplay_prendido_15_a_2,
       mantener_siplay_prendido_15_b_2, mantener_siplay_prendido_15_c_2, mantener_siplay_prendido_15_d_2,
       mantener_siplay_prendido_15_e, mantener_siplay_prendido_15_f, mantener_siplay_prendido_15_g,
       mantener_siplay_prendido_16_a_2, mantener_siplay_prendido_16_b_2, mantener_siplay_prendido_16_c_2,
       mantener_siplay_prendido_16_d_2, mantener_siplay_prendido_16_e, mantener_siplay_prendido_16_f,
       mantener_siplay_prendido_16_g, not_1_out, Reloj_out;
  wire [3:0] state_register_b4;

  _7_Segment_Display u_7_segment_display_1 (
    .g(mantener_siplay_prendido_1_d_2), .f(mantener_siplay_prendido_1_b_2),
    .a(mantener_siplay_prendido_1_a_2), .b(mantener_siplay_prendido_1_c_2), .e(mantener_siplay_prendido_1_e),
    .d(mantener_siplay_prendido_1_g), .c(mantener_siplay_prendido_1_f));  // open: dp
  decodificador_display decodificador_display_1 (
    .A(A), .B(B), .C(C), .D(D), .b_2(decodificador_display_1_b_2), .a_2(decodificador_display_1_a_2),
    .c_2(decodificador_display_1_c_2), .d_2(decodificador_display_1_d_2), .e(decodificador_display_1_e),
    .f(decodificador_display_1_f), .g(decodificador_display_1_g));
  mantener_siplay_prendido mantener_siplay_prendido_1 (
    .Reset(Reset), .Reloj(and_1_out), .a_2(mantener_siplay_prendido_1_a_2),
    .b_2(mantener_siplay_prendido_1_b_2), .c_2(mantener_siplay_prendido_1_c_2),
    .d_2(mantener_siplay_prendido_1_d_2), .e(mantener_siplay_prendido_1_e), .f(mantener_siplay_prendido_1_f),
    .g(mantener_siplay_prendido_1_g), .A(state_register_b4[3]), .B(state_register_b4[2]),
    .C(state_register_b4[1]), .D(state_register_b4[0]), .Enable(decoder_1_out5));
  _7_Segment_Display u_7_segment_display_2 (
    .g(mantener_siplay_prendido_2_d_2), .f(mantener_siplay_prendido_2_b_2),
    .a(mantener_siplay_prendido_2_a_2), .b(mantener_siplay_prendido_2_c_2), .e(mantener_siplay_prendido_2_e),
    .d(mantener_siplay_prendido_2_g), .c(mantener_siplay_prendido_2_f));  // open: dp
  mantener_siplay_prendido mantener_siplay_prendido_2 (
    .Reset(Reset), .Reloj(and_1_out), .a_2(mantener_siplay_prendido_2_a_2),
    .b_2(mantener_siplay_prendido_2_b_2), .c_2(mantener_siplay_prendido_2_c_2),
    .d_2(mantener_siplay_prendido_2_d_2), .e(mantener_siplay_prendido_2_e), .f(mantener_siplay_prendido_2_f),
    .g(mantener_siplay_prendido_2_g), .A(state_register_b4[3]), .B(state_register_b4[2]),
    .C(state_register_b4[1]), .D(state_register_b4[0]), .Enable(decoder_1_out14));
  _7_Segment_Display u_7_segment_display_3 (
    .g(mantener_siplay_prendido_3_d_2), .f(mantener_siplay_prendido_3_b_2),
    .a(mantener_siplay_prendido_3_a_2), .b(mantener_siplay_prendido_3_c_2), .e(mantener_siplay_prendido_3_e),
    .d(mantener_siplay_prendido_3_g), .c(mantener_siplay_prendido_3_f));  // open: dp
  mantener_siplay_prendido mantener_siplay_prendido_3 (
    .Reset(Reset), .Reloj(and_1_out), .a_2(mantener_siplay_prendido_3_a_2),
    .b_2(mantener_siplay_prendido_3_b_2), .c_2(mantener_siplay_prendido_3_c_2),
    .d_2(mantener_siplay_prendido_3_d_2), .e(mantener_siplay_prendido_3_e), .f(mantener_siplay_prendido_3_f),
    .g(mantener_siplay_prendido_3_g), .A(state_register_b4[3]), .B(state_register_b4[2]),
    .C(state_register_b4[1]), .D(state_register_b4[0]), .Enable(decoder_1_out15));
  _7_Segment_Display u_7_segment_display_4 (
    .g(decodificador_display_1_d_2), .f(decodificador_display_1_b_2), .a(decodificador_display_1_a_2),
    .b(decodificador_display_1_c_2), .e(decodificador_display_1_e), .d(decodificador_display_1_g),
    .c(decodificador_display_1_f));  // open: dp
  _7_Segment_Display u_7_segment_display_5 (
    .g(mantener_siplay_prendido_4_d_2), .f(mantener_siplay_prendido_4_b_2),
    .a(mantener_siplay_prendido_4_a_2), .b(mantener_siplay_prendido_4_c_2), .e(mantener_siplay_prendido_4_e),
    .d(mantener_siplay_prendido_4_g), .c(mantener_siplay_prendido_4_f));  // open: dp
  _7_Segment_Display u_7_segment_display_6 (
    .g(mantener_siplay_prendido_5_d_2), .f(mantener_siplay_prendido_5_b_2),
    .a(mantener_siplay_prendido_5_a_2), .b(mantener_siplay_prendido_5_c_2), .e(mantener_siplay_prendido_5_e),
    .d(mantener_siplay_prendido_5_g), .c(mantener_siplay_prendido_5_f));  // open: dp
  _7_Segment_Display u_7_segment_display_7 (
    .g(mantener_siplay_prendido_6_d_2), .f(mantener_siplay_prendido_6_b_2),
    .a(mantener_siplay_prendido_6_a_2), .b(mantener_siplay_prendido_6_c_2), .e(mantener_siplay_prendido_6_e),
    .d(mantener_siplay_prendido_6_g), .c(mantener_siplay_prendido_6_f));  // open: dp
  _7_Segment_Display u_7_segment_display_8 (
    .g(mantener_siplay_prendido_7_d_2), .f(mantener_siplay_prendido_7_b_2),
    .a(mantener_siplay_prendido_7_a_2), .b(mantener_siplay_prendido_7_c_2), .e(mantener_siplay_prendido_7_e),
    .d(mantener_siplay_prendido_7_g), .c(mantener_siplay_prendido_7_f));  // open: dp
  mantener_siplay_prendido mantener_siplay_prendido_4 (
    .Reset(Reset), .Reloj(and_1_out), .a_2(mantener_siplay_prendido_4_a_2),
    .b_2(mantener_siplay_prendido_4_b_2), .c_2(mantener_siplay_prendido_4_c_2),
    .d_2(mantener_siplay_prendido_4_d_2), .e(mantener_siplay_prendido_4_e), .f(mantener_siplay_prendido_4_f),
    .g(mantener_siplay_prendido_4_g), .A(state_register_b4[3]), .B(state_register_b4[2]),
    .C(state_register_b4[1]), .D(state_register_b4[0]), .Enable(decoder_1_out7));
  mantener_siplay_prendido mantener_siplay_prendido_5 (
    .Reset(Reset), .Reloj(and_1_out), .a_2(mantener_siplay_prendido_5_a_2),
    .b_2(mantener_siplay_prendido_5_b_2), .c_2(mantener_siplay_prendido_5_c_2),
    .d_2(mantener_siplay_prendido_5_d_2), .e(mantener_siplay_prendido_5_e), .f(mantener_siplay_prendido_5_f),
    .g(mantener_siplay_prendido_5_g), .A(state_register_b4[3]), .B(state_register_b4[2]),
    .C(state_register_b4[1]), .D(state_register_b4[0]), .Enable(decoder_1_out12));
  mantener_siplay_prendido mantener_siplay_prendido_6 (
    .Reset(Reset), .Reloj(and_1_out), .a_2(mantener_siplay_prendido_6_a_2),
    .b_2(mantener_siplay_prendido_6_b_2), .c_2(mantener_siplay_prendido_6_c_2),
    .d_2(mantener_siplay_prendido_6_d_2), .e(mantener_siplay_prendido_6_e), .f(mantener_siplay_prendido_6_f),
    .g(mantener_siplay_prendido_6_g), .A(state_register_b4[3]), .B(state_register_b4[2]),
    .C(state_register_b4[1]), .D(state_register_b4[0]), .Enable(decoder_1_out13));
  mantener_siplay_prendido mantener_siplay_prendido_7 (
    .Reset(Reset), .Reloj(and_1_out), .a_2(mantener_siplay_prendido_7_a_2),
    .b_2(mantener_siplay_prendido_7_b_2), .c_2(mantener_siplay_prendido_7_c_2),
    .d_2(mantener_siplay_prendido_7_d_2), .e(mantener_siplay_prendido_7_e), .f(mantener_siplay_prendido_7_f),
    .g(mantener_siplay_prendido_7_g), .A(state_register_b4[3]), .B(state_register_b4[2]),
    .C(state_register_b4[1]), .D(state_register_b4[0]), .Enable(decoder_1_out10));
  Recorrido_grafo state_register (
    .Reloj(Reloj_out), .Reset(Reset), .B1(state_register_b4[3]), .B2(state_register_b4[2]),
    .B3(state_register_b4[1]), .B4(state_register_b4[0]), .A(A), .B(B), .C(C), .D(D));
  decodificador_display decodificador_display_2 (
    .A(state_register_b4[3]), .B(state_register_b4[2]), .C(state_register_b4[1]), .D(state_register_b4[0]),
    .b_2(decodificador_display_2_b_2), .a_2(decodificador_display_2_a_2), .c_2(decodificador_display_2_c_2),
    .d_2(decodificador_display_2_d_2), .e(decodificador_display_2_e), .f(decodificador_display_2_f),
    .g(decodificador_display_2_g));
  Clock Reloj (.out(Reloj_out));
  _7_Segment_Display u_7_segment_display_9 (
    .g(mantener_siplay_prendido_8_d_2), .f(mantener_siplay_prendido_8_b_2),
    .a(mantener_siplay_prendido_8_a_2), .b(mantener_siplay_prendido_8_c_2), .e(mantener_siplay_prendido_8_e),
    .d(mantener_siplay_prendido_8_g), .c(mantener_siplay_prendido_8_f));  // open: dp
  mantener_siplay_prendido mantener_siplay_prendido_8 (
    .Reset(Reset), .Reloj(and_1_out), .a_2(mantener_siplay_prendido_8_a_2),
    .b_2(mantener_siplay_prendido_8_b_2), .c_2(mantener_siplay_prendido_8_c_2),
    .d_2(mantener_siplay_prendido_8_d_2), .e(mantener_siplay_prendido_8_e), .f(mantener_siplay_prendido_8_f),
    .g(mantener_siplay_prendido_8_g), .A(state_register_b4[3]), .B(state_register_b4[2]),
    .C(state_register_b4[1]), .D(state_register_b4[0]), .Enable(decoder_1_out6));
  _7_Segment_Display u_7_segment_display_10 (
    .g(mantener_siplay_prendido_9_d_2), .f(mantener_siplay_prendido_9_b_2),
    .a(mantener_siplay_prendido_9_a_2), .b(mantener_siplay_prendido_9_c_2), .e(mantener_siplay_prendido_9_e),
    .d(mantener_siplay_prendido_9_g), .c(mantener_siplay_prendido_9_f));  // open: dp
  mantener_siplay_prendido mantener_siplay_prendido_9 (
    .Reset(Reset), .Reloj(and_1_out), .a_2(mantener_siplay_prendido_9_a_2),
    .b_2(mantener_siplay_prendido_9_b_2), .c_2(mantener_siplay_prendido_9_c_2),
    .d_2(mantener_siplay_prendido_9_d_2), .e(mantener_siplay_prendido_9_e), .f(mantener_siplay_prendido_9_f),
    .g(mantener_siplay_prendido_9_g), .A(state_register_b4[3]), .B(state_register_b4[2]),
    .C(state_register_b4[1]), .D(state_register_b4[0]), .Enable(decoder_1_out9));
  _7_Segment_Display u_7_segment_display_11 (
    .g(mantener_siplay_prendido_10_d_2), .f(mantener_siplay_prendido_10_b_2),
    .a(mantener_siplay_prendido_10_a_2), .b(mantener_siplay_prendido_10_c_2),
    .e(mantener_siplay_prendido_10_e), .d(mantener_siplay_prendido_10_g), .c(mantener_siplay_prendido_10_f));  // open: dp
  mantener_siplay_prendido mantener_siplay_prendido_10 (
    .Reset(Reset), .Reloj(and_1_out), .a_2(mantener_siplay_prendido_10_a_2),
    .b_2(mantener_siplay_prendido_10_b_2), .c_2(mantener_siplay_prendido_10_c_2),
    .d_2(mantener_siplay_prendido_10_d_2), .e(mantener_siplay_prendido_10_e),
    .f(mantener_siplay_prendido_10_f), .g(mantener_siplay_prendido_10_g), .A(state_register_b4[3]),
    .B(state_register_b4[2]), .C(state_register_b4[1]), .D(state_register_b4[0]), .Enable(decoder_1_out11));
  _7_Segment_Display u_7_segment_display_12 (
    .g(decodificador_display_2_d_2), .f(decodificador_display_2_b_2), .a(decodificador_display_2_a_2),
    .b(decodificador_display_2_c_2), .e(decodificador_display_2_e), .d(decodificador_display_2_g),
    .c(decodificador_display_2_f));  // open: dp
  _7_Segment_Display u_7_segment_display_13 (
    .g(mantener_siplay_prendido_11_d_2), .f(mantener_siplay_prendido_11_b_2),
    .a(mantener_siplay_prendido_11_a_2), .b(mantener_siplay_prendido_11_c_2),
    .e(mantener_siplay_prendido_11_e), .d(mantener_siplay_prendido_11_g), .c(mantener_siplay_prendido_11_f));  // open: dp
  Decoder #(.select(4), .enable("false")) decoder_1 (
    .out0(decoder_1_out0), .out1(decoder_1_out1), .out2(decoder_1_out2), .out3(decoder_1_out3),
    .out4(decoder_1_out4), .out5(decoder_1_out5), .out6(decoder_1_out6), .out7(decoder_1_out7),
    .out8(decoder_1_out8), .out9(decoder_1_out9), .out10(decoder_1_out10), .out11(decoder_1_out11),
    .out12(decoder_1_out12), .out13(decoder_1_out13), .out14(decoder_1_out14), .out15(decoder_1_out15),
    .sel(state_register_b4));
  mantener_siplay_prendido mantener_siplay_prendido_11 (
    .Reset(Reset), .Reloj(and_1_out), .a_2(mantener_siplay_prendido_11_a_2),
    .b_2(mantener_siplay_prendido_11_b_2), .c_2(mantener_siplay_prendido_11_c_2),
    .d_2(mantener_siplay_prendido_11_d_2), .e(mantener_siplay_prendido_11_e),
    .f(mantener_siplay_prendido_11_f), .g(mantener_siplay_prendido_11_g), .A(state_register_b4[3]),
    .B(state_register_b4[2]), .C(state_register_b4[1]), .D(state_register_b4[0]), .Enable(decoder_1_out8));
  _7_Segment_Display u_7_segment_display_14 (
    .g(mantener_siplay_prendido_12_d_2), .f(mantener_siplay_prendido_12_b_2),
    .a(mantener_siplay_prendido_12_a_2), .b(mantener_siplay_prendido_12_c_2),
    .e(mantener_siplay_prendido_12_e), .d(mantener_siplay_prendido_12_g), .c(mantener_siplay_prendido_12_f));  // open: dp
  _7_Segment_Display u_7_segment_display_15 (
    .g(mantener_siplay_prendido_13_d_2), .f(mantener_siplay_prendido_13_b_2),
    .a(mantener_siplay_prendido_13_a_2), .b(mantener_siplay_prendido_13_c_2),
    .e(mantener_siplay_prendido_13_e), .d(mantener_siplay_prendido_13_g), .c(mantener_siplay_prendido_13_f));  // open: dp
  and and_1 (and_1_out, Reloj_out, not_1_out);
  not not_1 (not_1_out, d_ff_1_q);
  LED led_1 (.in(detector_de_final_1_end));
  detector_de_final detector_de_final_1 (
    .End(detector_de_final_1_end), .A(state_register_b4[3]), .B(state_register_b4[2]),
    .C(state_register_b4[1]), .D(state_register_b4[0]));
  mantener_siplay_prendido mantener_siplay_prendido_12 (
    .Reset(Reset), .Reloj(and_1_out), .a_2(mantener_siplay_prendido_12_a_2),
    .b_2(mantener_siplay_prendido_12_b_2), .c_2(mantener_siplay_prendido_12_c_2),
    .d_2(mantener_siplay_prendido_12_d_2), .e(mantener_siplay_prendido_12_e),
    .f(mantener_siplay_prendido_12_f), .g(mantener_siplay_prendido_12_g), .A(state_register_b4[3]),
    .B(state_register_b4[2]), .C(state_register_b4[1]), .D(state_register_b4[0]), .Enable(decoder_1_out3));
  mantener_siplay_prendido mantener_siplay_prendido_13 (
    .Reset(Reset), .Reloj(and_1_out), .a_2(mantener_siplay_prendido_13_a_2),
    .b_2(mantener_siplay_prendido_13_b_2), .c_2(mantener_siplay_prendido_13_c_2),
    .d_2(mantener_siplay_prendido_13_d_2), .e(mantener_siplay_prendido_13_e),
    .f(mantener_siplay_prendido_13_f), .g(mantener_siplay_prendido_13_g), .A(state_register_b4[3]),
    .B(state_register_b4[2]), .C(state_register_b4[1]), .D(state_register_b4[0]), .Enable(decoder_1_out4));
  D_Flip_Flop d_ff_1 (
    .clk(Reloj_out), .D(detector_de_final_1_end), .Q(d_ff_1_q), .en(1'b1), .reset(Reset));  // open: Qn, preset
  _7_Segment_Display u_7_segment_display_16 (
    .g(mantener_siplay_prendido_14_d_2), .f(mantener_siplay_prendido_14_b_2),
    .a(mantener_siplay_prendido_14_a_2), .b(mantener_siplay_prendido_14_c_2),
    .e(mantener_siplay_prendido_14_e), .d(mantener_siplay_prendido_14_g), .c(mantener_siplay_prendido_14_f));  // open: dp
  mantener_siplay_prendido mantener_siplay_prendido_14 (
    .Reset(Reset), .Reloj(and_1_out), .a_2(mantener_siplay_prendido_14_a_2),
    .b_2(mantener_siplay_prendido_14_b_2), .c_2(mantener_siplay_prendido_14_c_2),
    .d_2(mantener_siplay_prendido_14_d_2), .e(mantener_siplay_prendido_14_e),
    .f(mantener_siplay_prendido_14_f), .g(mantener_siplay_prendido_14_g), .A(state_register_b4[3]),
    .B(state_register_b4[2]), .C(state_register_b4[1]), .D(state_register_b4[0]), .Enable(decoder_1_out0));
  _7_Segment_Display u_7_segment_display_17 (
    .g(mantener_siplay_prendido_15_d_2), .f(mantener_siplay_prendido_15_b_2),
    .a(mantener_siplay_prendido_15_a_2), .b(mantener_siplay_prendido_15_c_2),
    .e(mantener_siplay_prendido_15_e), .d(mantener_siplay_prendido_15_g), .c(mantener_siplay_prendido_15_f));  // open: dp
  mantener_siplay_prendido mantener_siplay_prendido_15 (
    .Reset(Reset), .Reloj(and_1_out), .a_2(mantener_siplay_prendido_15_a_2),
    .b_2(mantener_siplay_prendido_15_b_2), .c_2(mantener_siplay_prendido_15_c_2),
    .d_2(mantener_siplay_prendido_15_d_2), .e(mantener_siplay_prendido_15_e),
    .f(mantener_siplay_prendido_15_f), .g(mantener_siplay_prendido_15_g), .A(state_register_b4[3]),
    .B(state_register_b4[2]), .C(state_register_b4[1]), .D(state_register_b4[0]), .Enable(decoder_1_out1));
  _7_Segment_Display u_7_segment_display_18 (
    .g(mantener_siplay_prendido_16_d_2), .f(mantener_siplay_prendido_16_b_2),
    .a(mantener_siplay_prendido_16_a_2), .b(mantener_siplay_prendido_16_c_2),
    .e(mantener_siplay_prendido_16_e), .d(mantener_siplay_prendido_16_g), .c(mantener_siplay_prendido_16_f));  // open: dp
  mantener_siplay_prendido mantener_siplay_prendido_16 (
    .Reset(Reset), .Reloj(and_1_out), .a_2(mantener_siplay_prendido_16_a_2),
    .b_2(mantener_siplay_prendido_16_b_2), .c_2(mantener_siplay_prendido_16_c_2),
    .d_2(mantener_siplay_prendido_16_d_2), .e(mantener_siplay_prendido_16_e),
    .f(mantener_siplay_prendido_16_f), .g(mantener_siplay_prendido_16_g), .A(state_register_b4[3]),
    .B(state_register_b4[2]), .C(state_register_b4[1]), .D(state_register_b4[0]), .Enable(decoder_1_out2));

  // Notes on the sheet:
  //   Bits de entrada
  //   F
  //   O
  //   P
  //   Nodo de entrada
  //   H
  //   M
  //   N
  //   K
  //   G
  //   J
  //   L
  //   Nodo actual
  //   I
  //   - Para resetear el circuito cambiar reset a 1 y luego devolverlo a cero para asegurar 
  //   que todo esté configurado correctamente
  //   D
  //   E
  //   Si la luz está encendida termina el recorrido de nodos
  //   A
  //   B
  //   C
endmodule

module decodificador_display (
  input  A,
  input  B,
  input  C,
  input  D,
  output a_2,
  output b_2,
  output c_2,
  output d_2,
  output e,
  output f,
  output g
);

  wire and_1_out, and_2_out, and_3_out, and_4_out, and_5_out, and_6_out, and_7_out, and_8_out, and_9_out,
       and_10_out, and_11_out, and_12_out, and_13_out, and_14_out, and_15_out, and_16_out, and_17_out,
       and_18_out, and_19_out, and_20_out, and_21_out, and_22_out, and_23_out, and_24_out, and_25_out,
       and_26_out, not_1_out, not_2_out, not_3_out, not_4_out, not_5_out, not_6_out, not_7_out, not_8_out,
       not_9_out, not_10_out, not_11_out, not_12_out, not_13_out, not_14_out, not_15_out, not_16_out,
       not_17_out, not_18_out, not_19_out, not_20_out, not_21_out, not_22_out, not_23_out, not_24_out,
       not_25_out, not_26_out, not_27_out, not_28_out, not_29_out, not_30_out, not_31_out, not_32_out,
       not_33_out, not_34_out, not_35_out, not_36_out;

  not not_1 (not_1_out, A);
  not not_2 (not_2_out, D);
  not not_3 (not_3_out, D);
  not not_4 (not_4_out, C);
  not not_5 (not_5_out, A);
  not not_6 (not_6_out, C);
  not not_7 (not_7_out, A);
  not not_8 (not_8_out, D);
  not not_9 (not_9_out, A);
  not not_10 (not_10_out, B);
  not not_11 (not_11_out, C);
  not not_12 (not_12_out, D);
  not not_13 (not_13_out, A);
  not not_14 (not_14_out, B);
  not not_15 (not_15_out, C);
  not not_16 (not_16_out, A);
  not not_17 (not_17_out, C);
  not not_18 (not_18_out, A);
  not not_19 (not_19_out, C);
  not not_20 (not_20_out, D);
  not not_21 (not_21_out, B);
  not not_22 (not_22_out, D);
  not not_23 (not_23_out, A);
  not not_24 (not_24_out, B);
  not not_25 (not_25_out, C);
  not not_26 (not_26_out, A);
  not not_27 (not_27_out, B);
  not not_28 (not_28_out, A);
  not not_29 (not_29_out, C);
  not not_30 (not_30_out, D);
  not not_31 (not_31_out, B);
  not not_32 (not_32_out, A);
  not not_33 (not_33_out, B);
  not not_34 (not_34_out, A);
  not not_35 (not_35_out, D);
  not not_36 (not_36_out, D);
  and and_1 (and_1_out, not_1_out, not_2_out);
  and and_2 (and_2_out, C, not_3_out);
  and and_3 (and_3_out, B, not_4_out);
  and and_4 (and_4_out, A, B);
  and and_5 (and_5_out, not_5_out, not_6_out);
  and and_6 (and_6_out, not_7_out, not_8_out);
  and and_7 (and_7_out, not_9_out, B);
  and and_8 (and_8_out, A, C);
  and and_9 (and_9_out, not_10_out, not_11_out, not_12_out);
  and and_10 (and_10_out, not_13_out, C, D);
  and and_11 (and_11_out, A, not_14_out, not_15_out);
  and and_12 (and_12_out, A, B, C);
  and and_13 (and_13_out, not_16_out, not_17_out);
  and and_14 (and_14_out, not_18_out, D);
  and and_15 (and_15_out, B, not_19_out, not_20_out);
  and and_16 (and_16_out, B, C, D);
  and and_17 (and_17_out, A, not_21_out, C, not_22_out);
  or or_1 (e, not_23_out, D, C, B);
  and and_18 (and_18_out, not_24_out, not_25_out);
  and and_19 (and_19_out, not_26_out, not_27_out, D);
  and and_20 (and_20_out, not_28_out, B, C);
  and and_21 (and_21_out, A, not_29_out);
  and and_22 (and_22_out, A, not_30_out);
  and and_23 (and_23_out, not_31_out, D);
  and and_24 (and_24_out, not_32_out, not_33_out, C);
  and and_25 (and_25_out, not_34_out, B, not_35_out);
  and and_26 (and_26_out, B, C, not_36_out);
  or or_2 (a_2, and_1_out, and_2_out, and_3_out, and_4_out);
  or or_3 (b_2, and_5_out, and_6_out, and_7_out, and_8_out);
  or or_4 (c_2, and_9_out, and_10_out, and_11_out, and_12_out);
  or or_5 (d_2, and_13_out, and_14_out, and_15_out, and_16_out, and_17_out);
  or or_6 (f, and_18_out, and_19_out, and_20_out, and_21_out, and_22_out);
  or or_7 (g, and_23_out, and_24_out, and_25_out, and_26_out);
  _7_Segment_Display u_7_segment_display_1 (.g(d_2), .f(b_2), .a(a_2), .b(c_2), .e(e), .d(g), .c(f));  // open: dp
endmodule

module Recorrido_grafo (
  input  Reloj,
  input  Reset,
  input  A,
  input  B,
  input  C,
  input  D,
  output B1,
  output B2,
  output B3,
  output B4
);

  wire d_ff_1_q, d_ff_2_q, d_ff_3_q, d_ff_4_q, d_ff_5_q, decodificador_display_1_a_2,
       decodificador_display_1_b_2, decodificador_display_1_c_2, decodificador_display_1_d_2,
       decodificador_display_1_e, decodificador_display_1_f, decodificador_display_1_g, display_decoder_a_2,
       display_decoder_b_2, display_decoder_c_2, display_decoder_d_2, display_decoder_e, display_decoder_f,
       display_decoder_g, multiplexer_1_out, multiplexer_2_out, multiplexer_3_out, multiplexer_4_out,
       next_node_logic_a2, next_node_logic_b2, next_node_logic_c2, next_node_logic_d2;

  _7_Segment_Display u_7_segment_display_1 (
    .g(decodificador_display_1_d_2), .f(decodificador_display_1_b_2), .a(decodificador_display_1_a_2),
    .b(decodificador_display_1_c_2), .e(decodificador_display_1_e), .d(decodificador_display_1_g),
    .c(decodificador_display_1_f));  // open: dp
  _7_Segment_Display u_7_segment_display_2 (
    .g(display_decoder_d_2), .f(display_decoder_b_2), .a(display_decoder_a_2), .b(display_decoder_c_2),
    .e(display_decoder_e), .d(display_decoder_g), .c(display_decoder_f));  // open: dp
  decodificador_display decodificador_display_1 (
    .A(A), .B(B), .C(C), .D(D), .b_2(decodificador_display_1_b_2), .a_2(decodificador_display_1_a_2),
    .c_2(decodificador_display_1_c_2), .d_2(decodificador_display_1_d_2), .e(decodificador_display_1_e),
    .f(decodificador_display_1_f), .g(decodificador_display_1_g));
  decodificador_display display_decoder (
    .A(B1), .B(B2), .C(B3), .D(B4), .b_2(display_decoder_b_2), .a_2(display_decoder_a_2),
    .c_2(display_decoder_c_2), .d_2(display_decoder_d_2), .e(display_decoder_e), .f(display_decoder_f),
    .g(display_decoder_g));
  D_Flip_Flop d_ff_1 (.clk(Reloj), .D(1'b1), .Q(d_ff_1_q), .en(1'b1), .reset(Reset));  // open: Qn, preset
  Multiplexer #(.enable("false")) multiplexer_1 (
    .in0(D), .in1(next_node_logic_d2), .out(multiplexer_1_out), .sel(d_ff_1_q));
  Multiplexer #(.enable("false")) multiplexer_2 (
    .in0(C), .in1(next_node_logic_c2), .out(multiplexer_2_out), .sel(d_ff_1_q));
  Multiplexer #(.enable("false")) multiplexer_3 (
    .in0(B), .in1(next_node_logic_b2), .out(multiplexer_3_out), .sel(d_ff_1_q));
  Multiplexer #(.enable("false")) multiplexer_4 (
    .in0(A), .in1(next_node_logic_a2), .out(multiplexer_4_out), .sel(d_ff_1_q));
  Multiplexer #(.enable("false")) multiplexer_5 (.in0(A), .in1(next_node_logic_a2), .out(B1), .sel(d_ff_1_q));
  Multiplexer #(.enable("false")) multiplexer_6 (.in0(B), .in1(next_node_logic_b2), .out(B2), .sel(d_ff_1_q));
  Multiplexer #(.enable("false")) multiplexer_7 (.in0(C), .in1(next_node_logic_c2), .out(B3), .sel(d_ff_1_q));
  Multiplexer #(.enable("false")) multiplexer_8 (.in0(D), .in1(next_node_logic_d2), .out(B4), .sel(d_ff_1_q));
  D_Flip_Flop d_ff_2 (.clk(Reloj), .D(multiplexer_1_out), .Q(d_ff_2_q), .en(1'b1), .reset(Reset));  // open: Qn, preset
  D_Flip_Flop d_ff_3 (.clk(Reloj), .D(multiplexer_2_out), .Q(d_ff_3_q), .en(1'b1), .reset(Reset));  // open: Qn, preset
  D_Flip_Flop d_ff_4 (.clk(Reloj), .D(multiplexer_3_out), .Q(d_ff_4_q), .en(1'b1), .reset(Reset));  // open: Qn, preset
  D_Flip_Flop d_ff_5 (.clk(Reloj), .D(multiplexer_4_out), .Q(d_ff_5_q), .en(1'b1), .reset(Reset));  // open: Qn, preset
  nodo_siguiente next_node_logic (
    .A1(d_ff_5_q), .B1(d_ff_4_q), .C1(d_ff_3_q), .D1(d_ff_2_q), .A2(next_node_logic_a2),
    .B2(next_node_logic_b2), .C2(next_node_logic_c2), .D2(next_node_logic_d2));

  // Notes on the sheet:
  //   Nodo de entrada
  //   Bits de entrada
  //   Nodo actual
  //   Bits de salida
endmodule

module nodo_siguiente (
  input  A1,
  input  B1,
  input  C1,
  input  D1,
  output A2,
  output B2,
  output C2,
  output D2
);

  wire and_1_out, and_2_out, and_3_out, and_4_out, and_5_out, and_6_out, and_7_out, and_8_out, and_9_out,
       and_10_out, and_11_out, and_12_out, and_13_out, and_14_out, and_15_out, and_16_out, not_1_out,
       not_2_out, not_3_out, not_4_out, not_5_out, not_6_out, not_7_out, not_8_out, not_9_out, not_10_out,
       not_11_out, not_12_out, not_13_out, not_14_out, not_15_out, not_16_out;

  not not_1 (not_1_out, A1);
  and and_1 (and_1_out, not_1_out, C1, D1);
  and and_2 (and_2_out, A1, not_2_out);
  not not_2 (not_2_out, B1);
  and and_3 (and_3_out, A1, not_3_out);
  not not_3 (not_3_out, C1);
  and and_4 (and_4_out, B1, D1);
  and and_5 (and_5_out, B1, C1);
  and and_6 (and_6_out, A1, D1);
  and and_7 (and_7_out, A1, C1);
  and and_8 (and_8_out, A1, B1);
  not not_4 (not_4_out, A1);
  not not_5 (not_5_out, B1);
  not not_6 (not_6_out, C1);
  not not_7 (not_7_out, A1);
  not not_8 (not_8_out, D1);
  not not_9 (not_9_out, C1);
  not not_10 (not_10_out, A1);
  and and_9 (and_9_out, not_10_out, not_11_out);
  not not_11 (not_11_out, C1);
  not not_12 (not_12_out, A1);
  and and_10 (and_10_out, not_12_out, not_13_out);
  not not_13 (not_13_out, D1);
  not not_14 (not_14_out, B1);
  and and_11 (and_11_out, not_14_out, not_15_out);
  not not_15 (not_15_out, D1);
  and and_12 (and_12_out, B1, not_16_out, D1);
  not not_16 (not_16_out, C1);
  and and_13 (and_13_out, A1, C1);
  or or_1 (A2, and_1_out, and_2_out, and_3_out);
  or or_2 (B2, and_4_out, and_5_out, and_6_out, and_7_out, and_8_out);
  and and_14 (and_14_out, not_4_out, not_5_out, not_6_out, D1);
  and and_15 (and_15_out, not_7_out, B1, not_8_out);
  or or_3 (C2, and_14_out, and_15_out, and_16_out);
  and and_16 (and_16_out, A1, B1, not_9_out);
  or or_4 (D2, and_9_out, and_10_out, and_11_out, and_12_out, and_13_out);

  // Notes on the sheet:
  //   Bits de un nodo
  //   Bits del siguiente nodo
endmodule

module detector_de_final (
  input  A,
  input  B,
  input  C,
  input  D,
  output End
);

  wire not_1_out, not_2_out;

  not not_1 (not_1_out, A);
  not not_2 (not_2_out, C);
  and and_1 (End, D, not_2_out, B, not_1_out);
endmodule

module mantener_siplay_prendido (
  input  A,
  input  B,
  input  C,
  input  D,
  input  Reset,
  input  Reloj,
  input  Enable,
  output a_2,
  output b_2,
  output c_2,
  output d_2,
  output e,
  output f,
  output g
);

  wire and_1_out, and_2_out, and_3_out, and_4_out, and_5_out, and_6_out, and_7_out, and_8_out, and_9_out,
       and_10_out, and_11_out, and_12_out, and_13_out, and_14_out, and_15_out, and_16_out, and_17_out,
       and_18_out, and_19_out, and_20_out, and_21_out, and_22_out, and_23_out, and_24_out, and_25_out,
       and_26_out, d_ff_1_q, multiplexer_1_out, multiplexer_2_out, multiplexer_3_out, multiplexer_4_out,
       multiplexer_5_out, multiplexer_6_out, multiplexer_7_out, not_1_out, not_2_out, not_3_out, not_4_out,
       not_5_out, not_6_out, not_7_out, not_8_out, not_9_out, not_10_out, not_11_out, not_12_out, not_13_out,
       not_14_out, not_15_out, not_16_out, not_17_out, not_18_out, not_19_out, not_20_out, not_21_out,
       not_22_out, not_23_out, not_24_out, not_25_out, not_26_out, not_27_out, not_28_out, not_29_out,
       not_30_out, not_31_out, not_32_out, not_33_out, not_34_out, not_35_out, not_36_out, or_1_out,
       or_2_out, or_3_out, or_4_out, or_5_out, or_6_out, or_7_out;

  not not_1 (not_1_out, A);
  not not_2 (not_2_out, D);
  not not_3 (not_3_out, D);
  not not_4 (not_4_out, C);
  not not_5 (not_5_out, A);
  not not_6 (not_6_out, C);
  not not_7 (not_7_out, A);
  not not_8 (not_8_out, D);
  not not_9 (not_9_out, A);
  not not_10 (not_10_out, B);
  not not_11 (not_11_out, C);
  not not_12 (not_12_out, D);
  not not_13 (not_13_out, A);
  not not_14 (not_14_out, B);
  not not_15 (not_15_out, C);
  not not_16 (not_16_out, A);
  not not_17 (not_17_out, C);
  not not_18 (not_18_out, A);
  not not_19 (not_19_out, C);
  not not_20 (not_20_out, D);
  not not_21 (not_21_out, B);
  not not_22 (not_22_out, D);
  not not_23 (not_23_out, A);
  not not_24 (not_24_out, B);
  not not_25 (not_25_out, C);
  not not_26 (not_26_out, A);
  not not_27 (not_27_out, B);
  not not_28 (not_28_out, A);
  not not_29 (not_29_out, C);
  not not_30 (not_30_out, D);
  not not_31 (not_31_out, B);
  not not_32 (not_32_out, A);
  not not_33 (not_33_out, B);
  not not_34 (not_34_out, A);
  not not_35 (not_35_out, D);
  not not_36 (not_36_out, D);
  and and_1 (and_1_out, not_1_out, not_2_out);
  and and_2 (and_2_out, C, not_3_out);
  and and_3 (and_3_out, B, not_4_out);
  and and_4 (and_4_out, A, B);
  and and_5 (and_5_out, not_5_out, not_6_out);
  and and_6 (and_6_out, not_7_out, not_8_out);
  and and_7 (and_7_out, not_9_out, B);
  and and_8 (and_8_out, A, C);
  and and_9 (and_9_out, not_10_out, not_11_out, not_12_out);
  and and_10 (and_10_out, not_13_out, C, D);
  and and_11 (and_11_out, A, not_14_out, not_15_out);
  and and_12 (and_12_out, A, B, C);
  and and_13 (and_13_out, not_16_out, not_17_out);
  and and_14 (and_14_out, not_18_out, D);
  and and_15 (and_15_out, B, not_19_out, not_20_out);
  and and_16 (and_16_out, B, C, D);
  and and_17 (and_17_out, A, not_21_out, C, not_22_out);
  or or_1 (or_1_out, not_23_out, D, C, B);
  and and_18 (and_18_out, not_24_out, not_25_out);
  and and_19 (and_19_out, not_26_out, not_27_out, D);
  and and_20 (and_20_out, not_28_out, B, C);
  and and_21 (and_21_out, A, not_29_out);
  and and_22 (and_22_out, A, not_30_out);
  and and_23 (and_23_out, not_31_out, D);
  and and_24 (and_24_out, not_32_out, not_33_out, C);
  and and_25 (and_25_out, not_34_out, B, not_35_out);
  and and_26 (and_26_out, B, C, not_36_out);
  or or_2 (or_2_out, and_1_out, and_2_out, and_3_out, and_4_out);
  or or_3 (or_3_out, and_5_out, and_6_out, and_7_out, and_8_out);
  or or_4 (or_4_out, and_9_out, and_10_out, and_11_out, and_12_out);
  or or_5 (or_5_out, and_13_out, and_14_out, and_15_out, and_16_out, and_17_out);
  or or_6 (or_6_out, and_18_out, and_19_out, and_20_out, and_21_out, and_22_out);
  or or_7 (or_7_out, and_23_out, and_24_out, and_25_out, and_26_out);
  D_Flip_Flop d_ff_1 (.clk(Reloj), .D(1'b1), .Q(d_ff_1_q), .en(Enable), .reset(Reset));  // open: Qn, preset
  Multiplexer #(.enable("false")) multiplexer_1 (.in0(or_2_out), .in1(a_2), .out(multiplexer_1_out), .sel(d_ff_1_q));
  Multiplexer #(.enable("false")) multiplexer_2 (.in0(or_3_out), .in1(b_2), .out(multiplexer_2_out), .sel(d_ff_1_q));
  Multiplexer #(.enable("false")) multiplexer_3 (.in0(or_4_out), .in1(c_2), .out(multiplexer_3_out), .sel(d_ff_1_q));
  Multiplexer #(.enable("false")) multiplexer_4 (.in0(or_5_out), .in1(d_2), .out(multiplexer_4_out), .sel(d_ff_1_q));
  Multiplexer #(.enable("false")) multiplexer_5 (.in0(or_1_out), .in1(e), .out(multiplexer_5_out), .sel(d_ff_1_q));
  Multiplexer #(.enable("false")) multiplexer_6 (.in0(or_6_out), .in1(f), .out(multiplexer_6_out), .sel(d_ff_1_q));
  Multiplexer #(.enable("false")) multiplexer_7 (.in0(or_7_out), .in1(g), .out(multiplexer_7_out), .sel(d_ff_1_q));
  D_Flip_Flop d_ff_2 (.clk(Reloj), .D(multiplexer_1_out), .Q(a_2), .en(Enable), .reset(Reset));  // open: Qn, preset
  D_Flip_Flop d_ff_3 (.clk(Reloj), .D(multiplexer_2_out), .Q(b_2), .en(Enable), .reset(Reset));  // open: Qn, preset
  D_Flip_Flop d_ff_4 (.clk(Reloj), .D(multiplexer_3_out), .Q(c_2), .en(Enable), .reset(Reset));  // open: Qn, preset
  D_Flip_Flop d_ff_5 (.clk(Reloj), .D(multiplexer_4_out), .Q(d_2), .en(Enable), .reset(Reset));  // open: Qn, preset
  D_Flip_Flop d_ff_6 (.clk(Reloj), .D(multiplexer_5_out), .Q(e), .en(Enable), .reset(Reset));  // open: Qn, preset
  D_Flip_Flop d_ff_7 (.clk(Reloj), .D(multiplexer_6_out), .Q(f), .en(Enable), .reset(Reset));  // open: Qn, preset
  D_Flip_Flop d_ff_8 (.clk(Reloj), .D(multiplexer_7_out), .Q(g), .en(Enable), .reset(Reset));  // open: Qn, preset
endmodule
